# Fritzing sketch DynamixelMITM (saved by Fritzing 1.0.1rc)
breadboards: 1

parts:
  Basys_1 = Digilent Basys 3 [part_number=XC7A35T-1CPG236C]
  Componente1 = Arduino Uno (Rev3) - ICSP
  J1 = Basic Servo
  VCC1 = Battery block 9V

nets:
  N1: Basys_1.3v3, Componente1.D1/TX
  GND: Basys_1.GND, Componente1.GND, J1.gnd, VCC1.-
  N2: Basys_1.JA10, J1.pulse
  N3: J1.vcc, VCC1.+

notes:
  Original controller
  Man-in-the-middle board
  Modified command
  Command sniffer

custom parts:
  Digilent Basys 3: The Basys 3 board is a complete, ready-to-use digital circuit development platform based on the latest Artix®-7 Field Programmable Gate Array (FPGA) from Xilinx®. With its high-capacity FPGA (Xilinx part number XC7A35T-1CPG236C), low overall cost, and collection of USB, VGA, and other ports, the Basys 3 can host designs ranging from introductory combinational circuits to complex sequential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
