# Fritzing sketch DynamixelFPGA (saved by Fritzing 1.0.1rc)
breadboards: 1

parts:
  Basys_1 = Digilent Basys 3 [part_number=XC7A35T-1CPG236C]
  VCC1 = Battery block 9V
  J1 = Basic Servo

nets:
  GND: Basys_1.GND, VCC1.-, J1.gnd
  N1: Basys_1.JA8, J1.pulse
  N2: VCC1.+, J1.vcc

notes:
  ON/OFF
  Selección de comando
  Angulo en grados
  Velocidad en rpm
  cable de datos bidireccional
  Dynamixel AX12-A

custom parts:
  Digilent Basys 3: The Basys 3 board is a complete, ready-to-use digital circuit development platform based on the latest Artix®-7 Field Programmable Gate Array (FPGA) from Xilinx®. With its high-capacity FPGA (Xilinx part number XC7A35T-1CPG236C), low overall cost, and collection of USB, VGA, and other ports, the Basys 3 can host designs ranging from introductory combinational circuits to complex sequential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
